# Fritzing sketch ESP32_SSD1306_U8g2 (saved by Fritzing 0.9.3b)
breadboards: 2

parts:
  MH-ET_LIVE_ESP32_DEVKIT1 = MH-ET LIVE ESP32 DEVKIT 38 pins
  Squix1 = OLED 0.96" 128x64 I2C SSD1306
  S1 = Pushbutton [package="[THT]"]
  S2 = Pushbutton [package="[THT]"]
  R1 = Resistor [tolerance=±5% resistance=220 package=THT]
  R2 = Resistor [tolerance=±5% resistance=220 package=THT]

nets:
  N1: MH-ET_LIVE_ESP32_DEVKIT1.3V3, S1.Pin_1, S1.Pin_2, S2.Pin_1, S2.Pin_2
  N2: MH-ET_LIVE_ESP32_DEVKIT1.SVP, S1.Pin_3, S1.Pin_4, R2.Pin_1
  N3: MH-ET_LIVE_ESP32_DEVKIT1.SVN, S2.Pin_3, S2.Pin_4, R1.Pin_1
  N4: MH-ET_LIVE_ESP32_DEVKIT1.GND#58, Squix1.GND, R1.Pin_0, R2.Pin_0
  5V: MH-ET_LIVE_ESP32_DEVKIT1.5V, Squix1.VCC
  N5: MH-ET_LIVE_ESP32_DEVKIT1.IO22, Squix1.SCL
  N6: MH-ET_LIVE_ESP32_DEVKIT1.IO21, Squix1.SCA

custom parts:
  MH-ET LIVE ESP32 DEVKIT 38 pins: http://mh.nodebb.com/topic/2/mh-et-live-esp32-devkit
